// Logisim project coa_final.circ as structural Verilog: 1 circuit, main circuit main
module main (
  input  [7:0] in_1,
  input  [7:0] Data_bits,
  input  [17:0] in_3,
  input  Store,
  input  [3:0] in_5,
  input  in_6,
  input  in_7,
  input  [7:0] in_8,
  input  in_9,
  input  [7:0] in_10,
  input  in_11,
  output [1:0] tag,
  output [1:0] block,
  output [7:0] out_14,
  output [7:0] out_15,
  output [7:0] out_16
);

  wire decoder_1_out0, decoder_1_out1, decoder_1_out2, decoder_1_out3, decoder_1_out4, decoder_1_out5,
       decoder_1_out6, decoder_1_out7, decoder_1_out8, decoder_1_out9, decoder_1_out10, decoder_1_out11,
       decoder_1_out12, decoder_1_out13, decoder_1_out14, decoder_1_out15, decoder_2_out0, decoder_2_out1,
       decoder_2_out2, decoder_2_out3, not_1_out, not_2_out;

  Decoder #(.select(4), .enable("false")) decoder_1 (
    .out0(decoder_1_out0), .out1(decoder_1_out1), .out2(decoder_1_out2), .out3(decoder_1_out3),
    .out4(decoder_1_out4), .out5(decoder_1_out5), .out6(decoder_1_out6), .out7(decoder_1_out7),
    .out8(decoder_1_out8), .out9(decoder_1_out9), .out10(decoder_1_out10), .out11(decoder_1_out11),
    .out12(decoder_1_out12), .out13(decoder_1_out13), .out14(decoder_1_out14), .out15(decoder_1_out15),
    .sel(in_5));
  not not_1 (not_1_out, Store);
  RAM #(.addrWidth(18), .bus("asynch")) ram_1 (
    .addr(in_3), .data(out_16), .sel(decoder_1_out0), .ld(not_1_out));  // open: clr
  RAM #(.addrWidth(18), .bus("asynch")) ram_2 (
    .addr(in_3), .data(out_16), .sel(decoder_1_out1), .ld(not_1_out));  // open: clr
  RAM #(.addrWidth(18), .bus("asynch")) ram_3 (
    .addr(in_3), .data(out_16), .sel(decoder_1_out2), .ld(not_1_out));  // open: clr
  RAM #(.addrWidth(18), .bus("asynch")) ram_4 (
    .addr(in_3), .data(out_16), .sel(decoder_1_out3), .ld(not_1_out));  // open: clr
  RAM #(.addrWidth(18), .bus("asynch")) ram_5 (
    .addr(in_3), .data(out_16), .sel(decoder_1_out4), .ld(not_1_out));  // open: clr
  RAM #(.addrWidth(18), .bus("asynch")) ram_6 (
    .addr(in_3), .data(out_16), .sel(decoder_1_out5), .ld(not_1_out));  // open: clr
  RAM #(.addrWidth(18), .bus("asynch")) ram_7 (
    .addr(in_3), .data(out_16), .sel(decoder_1_out6), .ld(not_1_out));  // open: clr
  RAM #(.addrWidth(18), .bus("asynch")) ram_8 (
    .addr(in_3), .data(out_16), .sel(decoder_1_out7), .ld(not_1_out));  // open: clr
  RAM #(.addrWidth(18), .bus("asynch")) ram_9 (
    .addr(in_3), .data(out_16), .sel(decoder_1_out8), .ld(not_1_out));  // open: clr
  RAM #(.addrWidth(18), .bus("asynch")) ram_10 (
    .addr(in_3), .data(out_16), .sel(decoder_1_out9), .ld(not_1_out));  // open: clr
  RAM #(.addrWidth(18), .bus("asynch")) ram_11 (
    .addr(in_3), .data(out_16), .sel(decoder_1_out10), .ld(not_1_out));  // open: clr
  RAM #(.addrWidth(18), .bus("asynch")) ram_12 (
    .addr(in_3), .data(out_16), .sel(decoder_1_out11), .ld(not_1_out));  // open: clr
  RAM #(.addrWidth(18), .bus("asynch")) ram_13 (
    .addr(in_3), .data(out_16), .sel(decoder_1_out12), .ld(not_1_out));  // open: clr
  RAM #(.addrWidth(18), .bus("asynch")) ram_14 (
    .addr(in_3), .data(out_16), .sel(decoder_1_out13), .ld(not_1_out));  // open: clr
  RAM #(.addrWidth(18), .bus("asynch")) ram_15 (
    .addr(in_3), .data(out_16), .sel(decoder_1_out14), .ld(not_1_out));  // open: clr
  RAM #(.addrWidth(18), .bus("asynch")) ram_16 (
    .addr(in_3), .data(out_16), .sel(decoder_1_out15), .ld(not_1_out));  // open: clr
  assign out_16 = Store ? in_1 : 8'bz;  // Controlled_Buffer controlled_buffer_1
  RAM #(.addrWidth(18), .bus("asynch")) ram_17 (
    .addr(in_3), .data(out_15), .sel(decoder_1_out0), .ld(not_1_out));  // open: clr
  RAM #(.addrWidth(18), .bus("asynch")) ram_18 (
    .addr(in_3), .data(out_15), .sel(decoder_1_out1), .ld(not_1_out));  // open: clr
  RAM #(.addrWidth(18), .bus("asynch")) ram_19 (
    .addr(in_3), .data(out_15), .sel(decoder_1_out2), .ld(not_1_out));  // open: clr
  RAM #(.addrWidth(18), .bus("asynch")) ram_20 (
    .addr(in_3), .data(out_15), .sel(decoder_1_out3), .ld(not_1_out));  // open: clr
  RAM #(.addrWidth(18), .bus("asynch")) ram_21 (
    .addr(in_3), .data(out_15), .sel(decoder_1_out4), .ld(not_1_out));  // open: clr
  RAM #(.addrWidth(18), .bus("asynch")) ram_22 (
    .addr(in_3), .data(out_15), .sel(decoder_1_out5), .ld(not_1_out));  // open: clr
  RAM #(.addrWidth(18), .bus("asynch")) ram_23 (
    .addr(in_3), .data(out_15), .sel(decoder_1_out6), .ld(not_1_out));  // open: clr
  RAM #(.addrWidth(18), .bus("asynch")) ram_24 (
    .addr(in_3), .data(out_15), .sel(decoder_1_out7), .ld(not_1_out));  // open: clr
  RAM #(.addrWidth(18), .bus("asynch")) ram_25 (
    .addr(in_3), .data(out_15), .sel(decoder_1_out8), .ld(not_1_out));  // open: clr
  RAM #(.addrWidth(18), .bus("asynch")) ram_26 (
    .addr(in_3), .data(out_15), .sel(decoder_1_out9), .ld(not_1_out));  // open: clr
  RAM #(.addrWidth(18), .bus("asynch")) ram_27 (
    .addr(in_3), .data(out_15), .sel(decoder_1_out10), .ld(not_1_out));  // open: clr
  RAM #(.addrWidth(18), .bus("asynch")) ram_28 (
    .addr(in_3), .data(out_15), .sel(decoder_1_out11), .ld(not_1_out));  // open: clr
  RAM #(.addrWidth(18), .bus("asynch")) ram_29 (
    .addr(in_3), .data(out_15), .sel(decoder_1_out12), .ld(not_1_out));  // open: clr
  RAM #(.addrWidth(18), .bus("asynch")) ram_30 (
    .addr(in_3), .data(out_15), .sel(decoder_1_out13), .ld(not_1_out));  // open: clr
  RAM #(.addrWidth(18), .bus("asynch")) ram_31 (
    .addr(in_3), .data(out_15), .sel(decoder_1_out14), .ld(not_1_out));  // open: clr
  RAM #(.addrWidth(18), .bus("asynch")) ram_32 (
    .addr(in_3), .data(out_15), .sel(decoder_1_out15), .ld(not_1_out));  // open: clr
  assign out_15 = Store ? Data_bits : 8'bz;  // Controlled_Buffer controlled_buffer_2
  BitSelector #(.width(4), .group(2)) bitselector_1 (.in(in_5), .out(tag), .sel(in_6));
  BitSelector #(.width(4), .group(2)) bitselector_2 (.in(in_5), .out(block), .sel(in_7));
  Hex_Digit_Display hex_digit_display_1 (.value({2'b00, tag}));  // open: dp
  Hex_Digit_Display hex_digit_display_2 (.value({2'b00, block}));  // open: dp
  Decoder #(.select(2), .enable("false")) decoder_2 (
    .out0(decoder_2_out0), .out1(decoder_2_out1), .out2(decoder_2_out2), .out3(decoder_2_out3), .sel(block));
  assign out_14 = in_9 ? in_8 : 8'bz;  // Controlled_Buffer controlled_buffer_3
  not not_2 (not_2_out, in_9);
  RAM #(.addrWidth(18), .bus("asynch")) ram_33 (
    .addr(in_3), .data(out_16), .sel(decoder_2_out0), .ld(not_1_out));  // open: clr
  RAM #(.addrWidth(18), .bus("asynch")) ram_34 (
    .addr(in_3), .data(out_16), .sel(decoder_2_out1), .ld(not_1_out));  // open: clr
  RAM #(.addrWidth(18), .bus("asynch")) ram_35 (
    .addr(in_3), .data(out_16), .sel(decoder_2_out2), .ld(not_1_out));  // open: clr
  RAM #(.addrWidth(18), .bus("asynch")) ram_36 (
    .addr(in_3), .data(out_16), .sel(decoder_2_out3), .ld(not_1_out));  // open: clr
  RAM #(.bus("asynch")) ram_37 (.addr(in_10), .data(out_14), .sel(in_11), .ld(not_2_out));  // open: clr
  RAM #(.addrWidth(18), .bus("asynch")) ram_38 (
    .addr(in_3), .data(out_15), .sel(decoder_2_out0), .ld(not_1_out));  // open: clr
  RAM #(.addrWidth(18), .bus("asynch")) ram_39 (
    .addr(in_3), .data(out_15), .sel(decoder_2_out1), .ld(not_1_out));  // open: clr
  RAM #(.addrWidth(18), .bus("asynch")) ram_40 (
    .addr(in_3), .data(out_15), .sel(decoder_2_out2), .ld(not_1_out));  // open: clr
  RAM #(.addrWidth(18), .bus("asynch")) ram_41 (
    .addr(in_3), .data(out_15), .sel(decoder_2_out3), .ld(not_1_out));  // open: clr

  // Notes on the sheet:
  //   address bits
  //   Main memory of sixe 4M*16
  //   Data bits
  //   Data out
  //   Data out
  //   Single unit RAM cell
  //   Cache of size 1K*16 
endmodule
